# Fritzing sketch schematic (saved by Fritzing 1.0.4)
breadboards: 1

parts:
  WeMos_D1_R1 = WeMos D1 R2
  Part1 = HT16K33 Breakout 16x8 LED Matrix Driver [part_number=1427]
  U1 = POT [knob_status=50% power=0.5W package=alps_pot]
  LED1 = smd LED [color="Red (633nm)" package="0805 [SMD]"]
  LED2 = smd LED [color="Yellow (595nm)" package="0805 [SMD]"]
  LED3 = smd LED [color="Green (570nm)" package="0805 [SMD]"]
  R1 = Resistor [tolerance=±5% resistance=220 package="1206 [SMD]"]
  R2 = Resistor [tolerance=±5% resistance=220 package="1206 [SMD]"]
  R3 = Resistor [tolerance=±5% resistance=220 package="1206 [SMD]"]
  S1 = Pushbutton [package="[THT]"]
  R4 = Resistor [tolerance=±5% power=0.25W resistance=10k package=THT]
  Yumo-enc1 = YumoE6B2
  M1 = DC Motor [voltage_(max)=6V voltage_(min)=3V]

nets:
  N1: WeMos_D1_R1.D0/RX, S1.Pin_3, S1.Pin_4, R4.Pin_0
  N2: WeMos_D1_R1.D3, LED1.anode
  N3: WeMos_D1_R1.D4, LED2.anode
  N4: WeMos_D1_R1.(D5), LED3.anode
  N5: WeMos_D1_R1.(D6), Yumo-enc1.A
  N6: WeMos_D1_R1.(D7), Yumo-enc1.B
  N7: WeMos_D1_R1.D8, M1.pin_1
  N8: WeMos_D1_R1.D14, Part1.SDA
  N9: WeMos_D1_R1.D15, Part1.SCL
  N10: WeMos_D1_R1.A0, U1.S
  GND: WeMos_D1_R1.GND, Part1.GND, U1.E, Yumo-enc1.GND, M1.pin_2
  5V: WeMos_D1_R1.5V, Part1.VDD, U1.A, R1.Pin_0, R2.Pin_0, R3.Pin_0, S1.Pin_1, S1.Pin_2, R4.Pin_1, Yumo-enc1.V
  N11: LED1.cathode, R1.Pin_1
  N12: LED2.cathode, R2.Pin_1
  N13: LED3.cathode, R3.Pin_1

custom parts:
  WeMos D1 R2: The D1 R2 is a mini wifi board based on the ESP-8266EX.
  HT16K33 Breakout 16x8 LED Matrix Driver: This is the magic sauce in our 7-segment and matrix backpacks, now available in breadboard-friendly breakout board format. The HT16K33 is a neat little chip that has the ability to drive a multiplexed 16x8 matrix (that's 128 individual LEDs). The communication protocol is I2C so it uses only 2 pins, and you can have up to 8 selectable I2C addresses so thats a total of 8 matrices, each one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
